// Logisim project IT012_Lab02_255218692.circ as structural Verilog
module Warm_up (
  input  [7:0] in_1,
  input  [7:0] in_2,
  output [7:0] out_3
);

  Adder adder_1 (.a(in_1), .b(in_2), .out(out_3));  // open: cin, cout
  // Probe on out_3
endmodule

module FA (
  input  Cin,
  input  B,
  input  A,
  output S,
  output Cout
);

  wire and_1_out, and_2_out, xor_2_out;

  and and_1 (and_1_out, A, B);
  xor xor_1 (S, A, B, Cin);
  xor xor_2 (xor_2_out, A, B);
  and and_2 (and_2_out, xor_2_out, Cin);
  or or_1 (Cout, and_2_out, and_1_out);
endmodule

module ADDSUB4 (
  input  [3:0] A,
  input  [3:0] B,
  input  SUB,
  output [3:0] out_4,
  output out_5
);

  wire fa_1_cout, fa_2_cout, fa_3_cout, xor_1_out, xor_2_out, xor_3_out, xor_4_out;

  // Probe on fa_1_cout
  FA fa_1 (.Cin(SUB), .B(xor_1_out), .A(A[0]), .S(out_4[0]), .Cout(fa_1_cout));
  // Probe on fa_2_cout
  FA fa_2 (.Cin(fa_1_cout), .B(xor_2_out), .A(A[1]), .S(out_4[1]), .Cout(fa_2_cout));
  xor xor_1 (xor_1_out, B[0], SUB);
  xor xor_2 (xor_2_out, B[1], SUB);
  xor xor_3 (xor_3_out, B[2], SUB);
  xor xor_4 (xor_4_out, B[3], SUB);
  // Probe on fa_3_cout
  FA fa_3 (.Cin(fa_2_cout), .B(xor_3_out), .A(A[2]), .S(out_4[2]), .Cout(fa_3_cout));
  FA fa_4 (.Cin(fa_3_cout), .B(xor_4_out), .A(A[3]), .S(out_4[3]), .Cout(out_5));
endmodule

module test (
  input  [3:0] A,
  input  [3:0] B,
  output [3:0] out_3,
  output out_4
);

  wire fa_1_cout, fa_2_cout, fa_3_cout;

  // Probe on fa_1_cout
  FA fa_1 (.Cin(1'b0), .B(B[0]), .A(A[0]), .S(out_3[0]), .Cout(fa_1_cout));
  // Probe on fa_2_cout
  FA fa_2 (.Cin(fa_1_cout), .B(B[1]), .A(A[1]), .S(out_3[1]), .Cout(fa_2_cout));
  // Probe on fa_3_cout
  FA fa_3 (.Cin(fa_2_cout), .B(B[2]), .A(A[2]), .S(out_3[2]), .Cout(fa_3_cout));
  FA fa_4 (.Cin(fa_3_cout), .B(B[3]), .A(A[3]), .S(out_3[3]), .Cout(out_4));
endmodule

module ALU8 (
  input  [2:0] OP,
  input  [7:0] B,
  input  [7:0] A,
  output LT,
  output Z,
  output out_6,
  output [7:0] R
);

  wire [7:0] adder_1_out, adder_2_out, and_1_out, multiplexer_1_out, multiplexer_2_out, not_1_out, or_1_out,
       subtractor_1_out, subtractor_2_out, xor_1_out;

  Adder adder_1 (.a(A), .b(B), .out(adder_1_out));  // open: cin, cout
  Adder adder_2 (.a(A), .b(8'h1), .out(adder_2_out));  // open: cin, cout
  Subtractor subtractor_1 (.a(A), .b(B), .out(subtractor_1_out));  // open: bin, bout
  Subtractor subtractor_2 (.a(A), .b(8'h1), .out(subtractor_2_out));  // open: bin, bout
  assign and_1_out = A & B;  // AND_Gate and_1, 8 bits wide
  assign or_1_out = A | B;  // OR_Gate or_1, 8 bits wide
  assign not_1_out = ~A;  // NOT_Gate not_1, 8 bits wide
  assign xor_1_out = A ^ B;  // XOR_Gate xor_1, 8 bits wide
  Multiplexer #(.select(2), .width(8)) multiplexer_1 (
    .in0(adder_1_out), .in1(adder_2_out), .in2(subtractor_1_out), .in3(subtractor_2_out),
    .out(multiplexer_1_out), .sel(OP[1:0]));  // open: en
  Multiplexer #(.select(2), .width(8)) multiplexer_2 (
    .in0(and_1_out), .in1(or_1_out), .in2(not_1_out), .in3(xor_1_out), .out(multiplexer_2_out));  // open: sel, en
  LT lt_1 (.R7(out_6), .B7(B[7]), .A7(A[7]), .LT(LT));
  Multiplexer #(.width(8)) multiplexer_3 (
    .in0(multiplexer_1_out), .in1(multiplexer_2_out), .out({out_6, R[6:0]}), .sel(OP[2]));  // open: en
  nor nor_1 (Z, R[0], R[1], R[2], R[3], R[4], R[5], R[6], out_6);

  assign R[7] = out_6;
endmodule

module LT (
  input  R7,
  input  B7,
  input  A7,
  output LT
);

  wire and_1_out, and_2_out, not_1_out, xnor_1_out;

  not not_1 (not_1_out, B7);
  and and_1 (and_1_out, A7, not_1_out);
  xnor xnor_1 (xnor_1_out, A7, B7);
  and and_2 (and_2_out, xnor_1_out, R7);
  or or_1 (LT, and_1_out, and_2_out);
endmodule

module DLATCH (
  input  D,
  input  E,
  output Q
);

  Multiplexer multiplexer_1 (.in0(Q), .in1(D), .out(Q), .sel(E));  // open: en
endmodule

module TN3 (
  input  D,
  input  CLK,
  output Q2,
  output out_4,
  output Q1,
  output out_6
);

  wire dlatch_1_q;

  D_Flip_Flop d_ff_1 (.clk(CLK), .D(D), .Q(out_4));  // open: Qn, preset, en, reset
  DLATCH dlatch_1 (.D(D), .E(CLK), .Q(dlatch_1_q));
  D_Flip_Flop d_ff_2 (.clk(CLK), .D(out_4), .Q(Q2));  // open: Qn, preset, en, reset
  DLATCH dlatch_2 (.D(dlatch_1_q), .E(CLK), .Q(Q1));

  assign out_6 = CLK;
endmodule

module REGFILE (
  input  CLK,
  input  WE,
  input  [1:0] RD,
  input  [7:0] DIN,
  input  [1:0] RA,
  input  [1:0] RB,
  output [7:0] R0,
  output [7:0] R2,
  output [7:0] R1,
  output [7:0] R3,
  output [7:0] QA,
  output [7:0] QB
);

  wire decoder_1_y0, decoder_1_y1, decoder_1_y2, decoder_1_y3;

  DECODER decoder_1 (
    .en(WE), .a(RD[1]), .b(RD[0]), .y0(decoder_1_y0), .y1(decoder_1_y1), .y2(decoder_1_y2), .y3(decoder_1_y3));
  Register register_1 (.D(DIN), .en(decoder_1_y0), .Q(R0), .clk(CLK));  // open: clr
  Register register_2 (.D(DIN), .en(decoder_1_y1), .Q(R2), .clk(CLK));  // open: clr
  Register register_3 (.D(DIN), .en(decoder_1_y2), .Q(R1), .clk(CLK));  // open: clr
  Register register_4 (.D(DIN), .en(decoder_1_y3), .Q(R3), .clk(CLK));  // open: clr
  Multiplexer #(.select(2), .width(8)) multiplexer_1 (
    .in0(R0), .in1(R1), .in2(R2), .in3(R3), .out(QA), .sel(RA));  // open: en
  Multiplexer #(.select(2), .width(8)) multiplexer_2 (
    .in0(R0), .in1(R1), .in2(R2), .in3(R3), .out(QB), .sel(RB));  // open: en
endmodule

module DECODER (
  input  en,
  input  a,
  input  b,
  output y0,
  output y1,
  output y2,
  output y3
);

  wire not_1_out, not_2_out;

  not not_1 (not_1_out, a);
  not not_2 (not_2_out, b);
  and and_1 (y0, not_2_out, not_1_out, en);
  and and_2 (y1, not_2_out, a, en);
  and and_3 (y2, b, not_1_out, en);
  and and_4 (y3, b, a, en);
endmodule

module DATAPATH (
  input  CLK,
  input  WE,
  input  SRC,
  input  [1:0] RD,
  input  [2:0] OP,
  input  [1:0] RA,
  input  [1:0] RB,
  input  [7:0] IMM,
  output [7:0] R3,
  output [7:0] R1,
  output [7:0] R2,
  output [7:0] R0,
  output [7:0] R,
  output Z
);

  wire [7:0] multiplexer_1_out, regfile_1_qa, regfile_1_qb;

  REGFILE regfile_1 (
    .CLK(CLK), .WE(WE), .RD(RD), .DIN(multiplexer_1_out), .RA(RA), .RB(RB), .R0(R0), .R2(R2), .R1(R1),
    .R3(R3), .QA(regfile_1_qa), .QB(regfile_1_qb));
  ALU8 alu8_1 (.OP(OP), .B(regfile_1_qb), .A(regfile_1_qa), .Z(Z), .R(R));  // open: LT, out_6
  Multiplexer #(.width(8)) multiplexer_1 (.in0(R), .in1(IMM), .out(multiplexer_1_out), .sel(SRC));  // open: en
endmodule
